# Fritzing sketch Diagrama_Conexión (saved by Fritzing 1.0.0rc)

parts:
  Componente1 = Arduino Uno (Rev3) - ICSP
  HC-SR04_Sensor_1 = HC-SR04 Ultrasonic Distance Sensor
  Grove1 = Grove OLED 128x96

nets:
  N1: Componente1.A4/SDA, Grove1.SDA
  N2: Componente1.A5/SCL, Grove1.SCL
  N3: Componente1.D9_PWM, HC-SR04_Sensor_1.TRIG
  N4: Componente1.D10_PWM/SS, HC-SR04_Sensor_1.ECHO
  VCC: Componente1.5V, HC-SR04_Sensor_1.VCC, Grove1.VCC
  GND: Componente1.GND, HC-SR04_Sensor_1.GND, Grove1.GND
